# Fritzing sketch DHT_photoresistor_CO (saved by Fritzing 0.9.2b)
breadboards: 1

parts:
  Part2 = Bluetooth HC-05 Macho
  DHT11_2 = DHT11 module
  Parte2 = MQ-7 breakout
  Part3 = KY-018 Photoresistor Module [package="Breakout board"]
  R1 = Resistor [tolerance=±5% resistance=2.2k package="0805 [SMD]"]
  R2 = Resistor [tolerance=±5% resistance=1k package="0805 [SMD]"]
  Parte3 = Arduino Uno (Rev3)

nets:
  N1: Part2.TXD, Parte3.D2
  N2: Part2.RXD, R1.Pin_0, R2.Pin_1
  VCC: Part2.VCC, DHT11_2.VCC, Parte2.VCC, Part3.Vin, Parte3.5V
  GND: Part2.GND, DHT11_2.GND, Parte2.GND, Part3.-, R1.Pin_1, Parte3.GND
  N3: DHT11_2.DATA, Parte3.D7
  N4: Parte2.AO, Parte3.A0
  N5: Part3.S, Parte3.A2
  N6: R2.Pin_0, Parte3.D3_PWM

custom parts:
  DHT11 module: DHT11 black pcb module
  MQ-7 breakout: SKU: 101282
  KY-018 Photoresistor Module: KY-018 Photoresistor module, used to measure light intensity. It can determine the presence or absence of light.
